# Fritzing sketch led (saved by Fritzing 0.9.5d)
breadboards: 1

parts:
  Part1 = Arduino Uno (Rev3)
  S1 = Pushbutton [package=THT]
  LED1 = RGB LED (com. cathode, rgb) [package="5 mm [THT]"]
  R1 = Resistor [tolerance=±5% resistance=220 package=THT]
  R2 = Resistor [tolerance=±5% resistance=220 package=THT]
  R3 = Photocell (LDR) [package=THT]
  RE1 = Rotary Encoder [package=THT]

nets:
  N1: Part1.A0, RE1.EncoderPinC
  N2: Part1.A1, R2.Pin_1, R3.pin_0
  N3: Part1.D8, S1.leg0
  N4: Part1.D9_PWM, R1.Pin_0
  N5: Part1.GND, S1.leg1, LED1.red_anode, R2.Pin_0, RE1.EncoderPinB
  N6: Part1.5V, R3.pin_1, RE1.EncoderPinA
  N7: LED1.green_anode, R1.Pin_1
